// Digital circuit signal generator and character indexer.dig as structural Verilog
module signal_generator_and_character_indexer (
  input  clk
);

  wire _7404_1_pin1, _7404_1_pin2, _7404_1_pin3, _7404_1_pin4, _7404_1_pin5, _7404_1_pin6, _7404_1_pin7,
       _7404_1_pin9, _7404_1_pin14, _7404_2_pin2, _7404_2_pin4, _7404_2_pin6, _7404_2_pin8, _7404_2_pin10,
       _7404_2_pin12, _7404_2_pin14, _7404_3_pin8, _7404_3_pin10, _7404_3_pin12, _7421_1_pin4, _7421_1_pin5,
       _7421_1_pin9, _7421_1_pin10, _7421_1_pin12, _7421_1_pin13, _7458_1_pin6, _7458_1_pin8, _7458_2_pin6,
       _7458_2_pin8, _74161_1_p1, _74161_1_p2, _74161_1_p4, _74161_1_p12, _74161_1_p16, _74161_1_p17,
       _74161_1_p18, _74161_1_p19, _74161_1_p20, _74161_2_pin11, _74161_2_pin14, _74161_3_pin2,
       _74161_3_pin3, _74161_3_pin10, _74161_3_pin13, _74161_3_pin15, _74161_5_pin6, _74161_5_pin10,
       _74161_5_pin11, _74161_5_pin12, _74161_5_pin13, _74161_5_pin14, _74161_5_pin15, _74161_7_pin14,
       _74161_8_p1, _74161_8_p2, _74161_8_p3, _744075_1_pin3, _744075_1_pin4, _744075_1_pin6, _744075_1_pin8,
       _744075_1_pin9, _744075_1_pin10, _744075_1_pin13, _744075_2_pin9, _744075_2_pin10, _744075_3_p1,
       _744075_3_p2, _744075_3_p4, _744075_3_p6, _744075_3_p7, _744075_3_p8, not_1_out, pxl;

  _7404 _7404_1 (
    .pin1(_7404_1_pin1), .pin2(_7404_1_pin2), .pin3(_7404_1_pin3), .pin4(_7404_1_pin4), .pin5(_7404_1_pin5),
    .pin6(_7404_1_pin6), .pin7(_7404_1_pin7), .pin9(_7404_1_pin9), .pin11(_7404_1_pin9),
    .pin13(_7404_1_pin9), .pin14(_7404_1_pin14));  // open: pin8, pin10, pin12
  // _74161 _74161_1: pin names not known; wires that end beside it: _74161_1_p1, _74161_1_p2, _74161_1_p1, _74161_1_p4, _7404_1_pin7, _7404_1_pin6, _7404_1_pin1, _7404_1_pin7, _7404_1_pin7, _7404_1_pin7, _7404_1_pin7, _74161_1_p12, _7404_1_pin7, _7404_1_pin14, _74161_1_p2, _74161_1_p16, _74161_1_p17, _74161_1_p18, _74161_1_p19, _74161_1_p20, _7404_1_pin14, _7404_1_pin14
  _7421 _7421_1 (
    .pin1(_74161_1_p19), .pin2(_74161_1_p12), .pin4(_7421_1_pin4), .pin5(_7421_1_pin5), .pin6(_7404_1_pin5),
    .pin8(_7404_1_pin3), .pin9(_7421_1_pin9), .pin10(_7421_1_pin10), .pin12(_7421_1_pin12),
    .pin13(_7421_1_pin13), .pin14(_7404_1_pin14));  // open: pin3, pin7, pin11
  _74161 _74161_2 (
    .pin1(_7404_1_pin6), .pin2(_7404_1_pin1), .pin3(_7404_1_pin7), .pin4(_7404_1_pin7), .pin5(_7404_1_pin7),
    .pin6(_7404_1_pin7), .pin7(_74161_1_p12), .pin8(_7404_1_pin7), .pin9(_7404_1_pin14),
    .pin10(_74161_1_p16), .pin11(_74161_2_pin11), .pin12(_7421_1_pin4), .pin13(_7421_1_pin5),
    .pin14(_74161_2_pin14), .pin16(_7404_1_pin14));  // open: pin15
  _74161 _74161_3 (
    .pin1(_7404_1_pin4), .pin2(_74161_3_pin2), .pin3(_74161_3_pin3), .pin4(_7404_1_pin7),
    .pin5(_7404_1_pin7), .pin6(_7404_1_pin7), .pin7(_74161_1_p12), .pin8(_7404_1_pin7), .pin9(_7404_1_pin14),
    .pin10(_74161_3_pin10), .pin11(_7421_1_pin12), .pin12(_7421_1_pin10), .pin13(_74161_3_pin13),
    .pin14(_7421_1_pin9), .pin15(_74161_3_pin15), .pin16(_7404_1_pin14));
  _74161 _74161_4 (
    .pin1(_7404_1_pin4), .pin2(_74161_3_pin2), .pin3(_74161_3_pin3), .pin4(_7404_1_pin7),
    .pin5(_7404_1_pin7), .pin6(_7404_1_pin7), .pin7(_74161_1_p12), .pin8(_7404_1_pin7), .pin9(_7404_1_pin14),
    .pin10(_74161_3_pin10), .pin11(_7421_1_pin12), .pin12(_7421_1_pin10), .pin13(_74161_3_pin13),
    .pin14(_7421_1_pin9), .pin15(_74161_3_pin15), .pin16(_7404_1_pin14));
  _74161 _74161_5 (
    .pin1(_7404_1_pin4), .pin2(_7404_1_pin6), .pin3(_7404_1_pin7), .pin4(_7404_1_pin7), .pin5(_7404_1_pin7),
    .pin6(_74161_5_pin6), .pin7(_74161_1_p12), .pin8(_7404_1_pin7), .pin9(_7404_1_pin14),
    .pin10(_74161_5_pin10), .pin11(_74161_5_pin11), .pin12(_74161_5_pin12), .pin13(_74161_5_pin13),
    .pin14(_74161_5_pin14), .pin15(_74161_5_pin15), .pin16(_7404_1_pin14));
  _74161 _74161_6 (
    .pin1(_7404_1_pin6), .pin2(_7404_1_pin7), .pin3(_7404_1_pin7), .pin4(_7404_1_pin7), .pin5(_74161_5_pin6),
    .pin6(_74161_1_p12), .pin7(_7404_1_pin7), .pin10(_7404_1_pin14), .pin11(_74161_5_pin10),
    .pin12(_74161_5_pin11), .pin13(_74161_5_pin12), .pin14(_74161_5_pin13), .pin15(_74161_5_pin14),
    .pin16(_74161_5_pin15));  // open: pin8, pin9
  _74161 _74161_7 (
    .pin1(_7404_1_pin4), .pin2(_7404_1_pin6), .pin3(_7404_1_pin7), .pin6(_7404_1_pin7), .pin7(_74161_1_p12),
    .pin8(_7404_1_pin7), .pin9(_7404_1_pin14), .pin10(_74161_5_pin15), .pin13(_7421_1_pin13),
    .pin14(_74161_7_pin14), .pin16(_7404_1_pin14));  // open: pin4, pin5, pin11, pin12, pin15
  not not_1 (not_1_out, _7421_1_pin13);
  // _74161 _74161_8: pin names not known; wires that end beside it: _74161_8_p1, _74161_8_p2, _74161_8_p3, _74161_8_p3
  _7404 _7404_2 (
    .pin1(_74161_1_p18), .pin2(_7404_2_pin2), .pin3(_74161_1_p19), .pin4(_7404_2_pin4), .pin5(_74161_1_p20),
    .pin6(_7404_2_pin6), .pin7(_74161_8_p1), .pin8(_7404_2_pin8), .pin9(_74161_2_pin14),
    .pin10(_7404_2_pin10), .pin11(_7421_1_pin5), .pin12(_7404_2_pin12), .pin13(_7421_1_pin4),
    .pin14(_7404_2_pin14));
  _744075 _744075_1 (
    .pin1(_7421_1_pin10), .pin2(_74161_5_pin14), .pin3(_744075_1_pin3), .pin4(_744075_1_pin4),
    .pin5(_74161_8_p1), .pin6(_744075_1_pin6), .pin7(_74161_8_p1), .pin8(_744075_1_pin8),
    .pin9(_744075_1_pin9), .pin10(_744075_1_pin10), .pin11(_744075_1_pin9), .pin12(_744075_1_pin6),
    .pin13(_744075_1_pin13), .pin14(_7404_2_pin14));
  _7404 _7404_3 (
    .pin1(_74161_3_pin13), .pin2(_744075_1_pin8), .pin3(_7421_1_pin12), .pin4(_744075_1_pin4),
    .pin5(_74161_5_pin13), .pin6(_744075_1_pin3), .pin7(_74161_8_p1), .pin8(_7404_3_pin8),
    .pin9(_74161_5_pin12), .pin10(_7404_3_pin10), .pin11(_74161_5_pin11), .pin12(_7404_3_pin12),
    .pin13(_74161_7_pin14), .pin14(_7404_2_pin14));
  _7458 _7458_1 (
    .pin1(not_1_out), .pin2(not_1_out), .pin3(_744075_1_pin3), .pin4(not_1_out), .pin5(_7404_3_pin8),
    .pin6(_7458_1_pin6), .pin7(_74161_8_p1), .pin8(_7458_1_pin8), .pin9(_7404_2_pin14),
    .pin10(_7404_3_pin12), .pin11(not_1_out), .pin12(_7404_2_pin14), .pin13(_7404_3_pin10),
    .pin14(_7404_2_pin14));
  Break break_1 ();  // open: brk
  _7458 _7458_2 (
    .pin1(_7404_2_pin2), .pin2(_7404_2_pin12), .pin3(_7404_2_pin14), .pin4(_7404_2_pin10),
    .pin5(_7404_2_pin8), .pin6(_7458_2_pin6), .pin7(1'b0), .pin8(_7458_2_pin8), .pin9(_74161_1_p20),
    .pin10(_74161_1_p19), .pin11(_74161_1_p18), .pin12(_7404_2_pin6), .pin13(_7404_2_pin4), .pin14(1'b1));
  _744075 _744075_2 (
    .pin1(_7404_2_pin12), .pin2(_7404_2_pin8), .pin3(_7404_3_pin8), .pin4(_7404_3_pin10),
    .pin5(_7404_3_pin12), .pin6(_744075_1_pin13), .pin7(1'b0), .pin8(_7458_2_pin8), .pin9(_744075_2_pin9),
    .pin10(_744075_2_pin10), .pin11(_74161_8_p1), .pin12(_7458_1_pin8), .pin13(_7458_1_pin6), .pin14(1'b1));
  // _74161 _74161_9: pin names not known; wires that end beside it: _7404_2_pin14
  // _744075 _744075_3: pin names not known; wires that end beside it: _744075_3_p1, _744075_3_p2, _744075_3_p2, _744075_3_p4, _744075_3_p1, _744075_3_p6, _744075_3_p7, _744075_3_p8, _744075_3_p7, _744075_3_p8, _744075_3_p6, _744075_2_pin10
  VGA vga_1 (.R(1'b0), .G(1'b0), .B(_7404_2_pin14), .H(_744075_2_pin9), .V(_744075_1_pin10), .C(pxl));

  // Notes on the sheet:
  //   clk: Current line vertical (0-524)
  //   Frame completion pulse
  //   Horizontal character counter
  //   Pixel clock divider
  //   Line completion pulse
  //   Line counter
  //   Low during hsync
  //   3 lines below are also character
  //   pixel vertical
  //   Shifting current line bus left 3 bits
  //   should also give current vertical
  //   character
  //   !C
  //   !G
  //   !E
  //   !F
  //   High during hvis
  //   High during vvis
  //   Low during vsync
  //   Can the pulsegen be made smaller?
  //   Probably. Front/back porch do
  //   not need to be pulsed.
  //   All we want is:
  //   - hsync line that goes low during hsync, stays high else
  //   - vis line that goes low during blanking, stays high else
endmodule
